# Fritzing sketch 7-segments (saved by Fritzing 0.9.2b)
breadboards: 1

parts:
  Part1 = Arduino Uno (Rev3) - ICSP
  DI1 = 7-Segment LED Display [package=THT]
  R1 = Resistor [tolerance=±5% resistance=220 package="2010 [SMD]"]

nets:
  N1: Part1.ICSP_MISO, Part1.D12/MISO, DI1.cathodeF
  N2: Part1.ICSP_MOSI, Part1.D11_PWM/MOSI, DI1.cathodeE
  N3: Part1.D8, DI1.cathodeB
  N4: Part1.D9_PWM, DI1.cathodeC
  N5: Part1.D10_PWM/SS, DI1.cathodeD
  N6: Part1.D13/SCK, DI1.cathodeG
  N7: Part1.D7, DI1.cathodeA
  N8: Part1.5V, R1.Pin_0
  N9: DI1.commAnode#7, R1.Pin_1
